// Logisim project digitalSimulation.circ as structural Verilog: 2 circuits, main circuit digital simulation
module digital_simulation (
  input  in_1,
  input  in_2,
  input  in_3,
  input  _32_beat_bearings,
  input  in_5,
  input  in_6,
  input  in_7,
  input  in_8,
  input  in_9,
  input  in_10,
  input  in_11,
  input  in_12,
  input  in_13,
  input  in_14,
  input  in_15,
  input  in_16,
  input  A0_1,
  input  A1_1,
  input  A2_1,
  input  A3_1,
  input  in_21,
  input  in_22,
  input  in_23,
  input  in_24,
  input  in_25,
  input  in_26,
  input  in_27,
  input  in_28,
  input  in_29,
  input  in_30,
  input  in_31,
  input  in_32,
  input  in_33,
  input  in_34,
  input  in_35,
  input  in_36,
  input  A0_2,
  input  A1_2,
  input  A2_2,
  input  A3_2,
  output z_1,
  output z_2
);

  Multiplexer #(.select(4), .disabled(0), .enable("false")) multiplexer_1 (
    .in0(in_8), .in1(in_7), .in2(in_6), .in3(in_5), .in4(_32_beat_bearings), .in5(in_3), .in6(in_2),
    .in7(in_1), .in8(in_16), .in9(in_15), .in10(in_14), .in11(in_13), .in12(in_12), .in13(in_11),
    .in14(in_10), .in15(in_9), .out(z_1), .sel({A3_1, A2_1, A1_1, A0_1}));
  Multiplexer #(.select(4), .disabled(0), .enable("false")) multiplexer_2 (
    .in0(in_28), .in1(in_27), .in2(in_26), .in3(in_25), .in4(in_24), .in5(in_23), .in6(in_22), .in7(in_21),
    .in8(in_36), .in9(in_35), .in10(in_34), .in11(in_33), .in12(in_32), .in13(in_31), .in14(in_30),
    .in15(in_29), .out(z_2), .sel({A3_2, A2_2, A1_2, A0_2}));

  // Notes on the sheet:
  //   Arduino Variable Names
endmodule

module analog_pull_down_resistors (
  input  _8_beat_bearings,
  input  in_2,
  input  in_3,
  input  in_4,
  input  in_5,
  input  in_6,
  input  in_7,
  input  in_8,
  input  _8_beat_bearings_2,
  input  in_10,
  input  in_11,
  input  in_12,
  input  in_13,
  input  in_14,
  input  in_15,
  input  in_16,
  input  A0_1,
  input  A1_1,
  input  A2_1,
  input  A3_1,
  output out_21
);

  Pull_Resistor pull_resistor_1 (.node(_8_beat_bearings));
  Pull_Resistor pull_resistor_2 (.node(in_2));
  Pull_Resistor pull_resistor_3 (.node(in_3));
  Pull_Resistor pull_resistor_4 (.node(in_4));
  Pull_Resistor pull_resistor_5 (.node(in_12));
  Pull_Resistor pull_resistor_6 (.node(_8_beat_bearings_2));
  Pull_Resistor pull_resistor_7 (.node(in_10));
  Pull_Resistor pull_resistor_8 (.node(in_11));
  Pull_Resistor pull_resistor_9 (.node(in_8));
  Pull_Resistor pull_resistor_10 (.node(in_6));
  Pull_Resistor pull_resistor_11 (.node(in_5));
  Pull_Resistor pull_resistor_12 (.node(in_7));
  Pull_Resistor pull_resistor_13 (.node(in_15));
  Pull_Resistor pull_resistor_14 (.node(in_16));
  Pull_Resistor pull_resistor_15 (.node(in_14));
  Pull_Resistor pull_resistor_16 (.node(in_13));
  Multiplexer #(.select(4), .disabled(0), .enable("false")) multiplexer_1 (
    .in0(in_8), .in1(in_7), .in2(in_6), .in3(in_5), .in4(in_4), .in5(in_3), .in6(in_2),
    .in7(_8_beat_bearings), .in8(in_16), .in9(in_15), .in10(in_14), .in11(in_13), .in12(in_12), .in13(in_11),
    .in14(in_10), .in15(_8_beat_bearings_2), .out(out_21), .sel({A3_1, A2_1, A1_1, A0_1}));
endmodule
